# Fritzing sketch Untitled Sketch (saved by Fritzing 0.9.3b)
breadboards: 1

parts:
  Εξάρτημα1 = Triple Axis Accelerometer Breakout - ADXL335
  Εξάρτημα2 = Arduino Leonardo (Rev3b)
  Raspberry_Pi3 = Raspberry Pi B+  # not connected

nets:
  N1: Εξάρτημα1.ZOUT, Εξάρτημα2.A2
  N2: Εξάρτημα1.YOUT, Εξάρτημα2.A1
  N3: Εξάρτημα1.XOUT, Εξάρτημα2.A0
  VCC: Εξάρτημα1.VCC, Εξάρτημα2.3V3, Εξάρτημα2.AREF
